# Fritzing sketch PSoC 4 Pioneer Kit UART配線 (saved by Fritzing 0.9.2b)
perfboards: 3

parts:
  J1 = female pin header, 9 pins [form="♀ (female)"]  # not connected
  J2 = female pin header, 9 pins [form="♀ (female)"]  # not connected
  J3 = female pin header, 8 pins [form="♀ (female)"]  # not connected
  J4 = female pin header, 8 pins [form="♀ (female)"]
  J6 = female pin header, 6 pins [form="♀ (female)"]
  J7 = female pin header, 6 pins [form="♀ (female)"]
  J5 = female pin header, 10 pins [form="♀ (female)"]  # not connected
  J8 = female pin header, 9 pins [form="♀ (female)"]  # not connected
  J9 = female pin header, 9 pins [form="♀ (female)"]  # not connected
  J10 = female pin header, 10 pins [form="♀ (female)"]
  J11 = female pin header, 8 pins [form="♀ (female)"]  # not connected
  J12 = female pin header, 8 pins [form="♀ (female)"]  # not connected
  J13 = female pin header, 6 pins [form="♀ (female)"]
  J14 = female pin header, 6 pins [form="♀ (female)"]
  J15 = female pin header, 9 pins [form="♀ (female)"]  # not connected
  J16 = female pin header, 9 pins [form="♀ (female)"]  # not connected
  J17 = female pin header, 8 pins [form="♀ (female)"]  # not connected
  J18 = female pin header, 8 pins [form="♀ (female)"]  # not connected
  J19 = female pin header, 10 pins [form="♀ (female)"]
  J20 = female pin header, 6 pins [form="♀ (female)"]
  J21 = female pin header, 6 pins [form="♀ (female)"]

nets:
  N1: J4.pin1, J7.pin2
  N2: J4.pin2, J6.pin2
  N3: J10.pin9, J14.pin2
  N4: J10.pin10, J13.pin2
  N5: J19.pin4, J21.pin2
  N6: J19.pin5, J20.pin2

notes:
  PSoC 4 Pioneer Kit
  UART:RX P0[4]
  UART:TX P0[5]
  PSoC 4 Pioneer Kit
  UART:RX P4[0]
  UART:TX P4[1]
  RX
  TX
  PSoC 4 Pioneer Kit
  UART:RX P3[0]
  UART:TX P3[1]
